# Fritzing sketch electrical_schematic (saved by Fritzing 0.9.3b)

parts:
  LED1 = smd LED [color="Green (555nm)" package="0805 [SMD]"]
  LED2 = smd LED [color="Red (633nm)" package="0805 [SMD]"]
  LED3 = smd LED [color="Red (633nm)" package="0805 [SMD]"]
  LED4 = smd LED [color="Red (633nm)" package="0805 [SMD]"]
  LED5 = smd LED [color="Red (633nm)" package="0805 [SMD]"]
  Part1 = Arduino Uno (Rev3)
  R1 = Resistor [tolerance=±5% resistance=220 package="2512 [SMD]"]
  R2 = Resistor [tolerance=±5% resistance=220 package="2512 [SMD]"]
  R3 = Resistor [tolerance=±5% resistance=220 package="2512 [SMD]"]
  R4 = Resistor [tolerance=±5% resistance=220 package="2512 [SMD]"]
  R5 = Resistor [tolerance=±5% resistance=220 package="2512 [SMD]"]
  S1 = Momentary Switch [package=ksa_sealed_tac_switch]
  J1 = shrouded pin header, 10 pins [form="♂ (shrouded male)"]
  R6 = Resistor [tolerance=±5% resistance=220 package="2512 [SMD]"]
  J2 = shrouded pin header, 10 pins [form="♂ (shrouded male)"]
  S2 = H-Bridge with L298N
  U1 = LIPO-110mAh [package=lipo-110]
  Motor/Encoder_2 = DC Motor with two-phase hall-encoder [part_number=VT-E-G25A-06-177E]
  Motor/Encoder_1 = DC Motor with two-phase hall-encoder [part_number=VT-E-G25A-06-177E]
  Part4 = SRF05 Ultrasonic Rangefinder
  J3 = shrouded pin header, 10 pins [form="♂ (shrouded male)"]
  Part5 = SRF05 Ultrasonic Rangefinder
  Part6 = SRF05 Ultrasonic Rangefinder
  J4 = shrouded pin header, 10 pins [form="♂ (shrouded male)"]

nets:
  N1: LED1.cathode, J1.pin1
  N2: LED1.anode, R5.Pin_0
  N3: LED2.cathode, J1.pin2, J1.pin9
  N4: LED2.anode, R4.Pin_0
  N5: LED3.cathode, J1.pin3, J1.pin8
  N6: LED3.anode, R3.Pin_0
  N7: LED4.cathode, J1.pin4, J1.pin7
  N8: LED4.anode, R1.Pin_0
  N9: LED5.cathode, J1.pin5, J1.pin6
  N10: LED5.anode, R2.Pin_0
  N11: Part1.A0, R6.Pin_1
  N12: Part1.A1, R2.Pin_1
  N13: Part1.A2, R1.Pin_1
  N14: Part1.A3, R3.Pin_1
  N15: Part1.A4/SDA, R4.Pin_1
  N16: Part1.A5/SCL, R5.Pin_1
  N17: Part1.D8, S2.IN2
  N18: Part1.D9_PWM, S2.IN1
  N19: Part1.D10_PWM/SS, S2.ENA
  N20: Part1.D11_PWM/MOSI, Part6.Trig, Part6.Echo
  N21: Part1.D12/MISO, Part4.Trig, Part4.Echo
  N22: Part1.D13/SCK, Part5.Trig, Part5.Echo
  N23: Part1.GND, J1.pin10, J2.pin6, J4.pin4
  N24: Part1.D0/RX, Motor/Encoder_2.pin6
  N25: Part1.D2, Motor/Encoder_2.pin5
  N26: Part1.D3_PWM, Motor/Encoder_1.pin5
  N27: Part1.D4, Motor/Encoder_1.pin6
  N28: Part1.D5_PWM, S2.ENB
  N29: Part1.D6_PWM, S2.IN4
  N30: Part1.D7, S2.IN3
  N31: Part1.5V, J3.pin6
  N32: S1.1, J2.pin1
  N33: S1.2, R6.Pin_0
  N34: S2.12V, U1.+
  N35: S2.GND, J4.pin1
  N36: S2.5V, J3.pin10
  N37: S2.M1-01, Motor/Encoder_1.pin1
  N38: S2.M1-02, Motor/Encoder_1.pin2
  N39: S2.M2-01, Motor/Encoder_2.pin1
  N40: S2.M2-02, Motor/Encoder_2.pin2
  N41: U1.-, J4.pin10
  N42: Motor/Encoder_2.pin3, J3.pin1
  N43: Motor/Encoder_2.pin4, J4.pin3
  N44: Motor/Encoder_1.pin3, J3.pin2
  N45: Motor/Encoder_1.pin4, J4.pin2
  N46: Part4.VCC, J3.pin4
  N47: Part4.GND, J4.pin6
  N48: J3.pin3, Part6.VCC
  N49: J3.pin5, Part5.VCC
  N50: Part5.GND, J4.pin5
  N51: Part6.GND, J4.pin7

custom parts:
  H-Bridge with L298N: h-bridge
